# Fritzing sketch common (saved by Fritzing 0.9.3b)
breadboards: 2

parts:
  U1 = NodeMCU V1.0
  U3 = RELAY [package=relay-jzc]
  LED1 = LEDs [package=led10mm]
  D1 = SOLAR-IXYS [package=solarbit-12x1]
  U4 = LIPO-2000mAh [package=lipo-2000]
  U5 = RELAY [package=relay-jzc]
  U6 = RELAY [package=relay-jzc]
  U8 = RELAY [package=relay-jzc]
  U7 = RELAY [package=relay-jzc]
  Part1 = Logic Level Converter
  Part2 = Logic Level Converter
  Part3 = Logic Level Converter
  Part4 = Logic Level Converter
  M1 = DC Motor
  DHT1 = DHT22 Humidity and Temperature Sensor
  IC1 = Switching step-up voltage regulator [package=sot23-5]
  IC2 = Switching step-up voltage regulator [package=sot23-5]
  U9 = GAS_SENSOR [package=mq-3]
  IC3 = Switching step-up voltage regulator [package=sot23-5]
  IC4 = Switching step-up voltage regulator [package=sot23-5]
  U10 = LIPO-2000mAh [package=lipo-2000]
  D2 = SOLAR-IXYS [package=solarbit-12x1]
  U11 = NodeMCU V1.0
  Part5 = Logic Level Converter
  Grove2 = Grove Light Sensor
  PIR2 = PIR sensor
  J2 = Piezo Speaker

nets:
  N1: U1.D0, Part1.TX2_LV
  N2: U1.D1, Part2.RX_LV
  N3: U1.D2, Part2.TX2_LV
  N4: U1.D4, U8.NO, Part3.GND
  N5: U1.D5, Part4.RX_LV
  N6: U1.D6, Part4.TX2_LV
  N7: U1.D7, Part1.RX_LV
  N8: U1.Vin, U3.COIL1, IC2.LX
  GND: U1.GND, IC2.GND, PIR2.GND
  N9: U1.A0, Part3.TX2_LV
  N10: U3.COIL2, U6.COIL2, U8.COIL2, U7.COIL2, DHT1.VDD, IC1.LX
  N11: U3.NC, U5.COIL1, U6.NC, U8.NC, U7.NC, IC1.GND
  N12: U3.NO, Part4.TX2_HV
  N13: U3.MAIN, PIR2.VDD
  N14: LED1.A, U7.MAIN
  N15: D1.A, U4.+, IC1.OUT, IC2.EN, IC2.OUT, U9.H2
  N16: D1.C, U4.-, U8.COIL1, IC1.NC, IC2.NC
  N17: U5.NO, Part1.TX2_HV
  N18: U5.MAIN, DHT1.GND
  N19: U6.NO, Part2.RX_HV
  N20: U6.MAIN, M1.pin_2
  N21: U8.MAIN, U9.H1
  N22: U7.NO, Part2.TX2_HV
  N23: Part1.RX_HV, DHT1.DATA
  N24: Part3.TX2_HV, U9.A1
  N25: Part4.RX_HV, PIR2.SIG
  N26: IC3.OUT, IC4.EN, IC4.OUT, U10.+, D2.A, Grove2.VCC
  N27: IC3.NC, IC4.NC, U10.-, D2.C, Grove2.GND
  GND_2: IC4.GND, U11.GND, J2.pin1
  N28: IC4.LX, U11.Vin
  N29: U11.D0, J2.pin2
  N30: U11.D1, Part5.RX2_LV
  N31: Part5.RX2_HV, Grove2.SIG

notes:
  PIR Motion Sensor
  Light Control
  Fan Control
  Smoke Sensor
  Dht22 Temperature & Humidity Sensor
  AC ~
  12V DC
  Photocell Sensor Sensor

custom parts:
  NodeMCU V1.0: ESP9266 based NodeMCU
  Grove Light Sensor: An analog light sensor
