# Fritzing sketch livingRoom (saved by Fritzing 0.9.3b)
breadboards: 1

parts:
  U1 = NodeMCU V1.0
  U2 = MLX90614 [package=to-39]
  U3 = RELAY [package=relay-jzc]
  LED1 = LEDs [package=led10mm]
  JP1 = Header 2 [package=jst-2-pth]
  D1 = SOLAR-IXYS [package=solarbit-12x1]
  U4 = LIPO-2000mAh [package=lipo-2000]
  U5 = RELAY [package=relay-jzc]
  U6 = RELAY [package=relay-jzc]
  U8 = RELAY [package=relay-jzc]
  U7 = RELAY [package=relay-jzc]
  Part1 = Logic Level Converter
  Part2 = Logic Level Converter
  Part3 = Logic Level Converter
  Part4 = Logic Level Converter
  M1 = DC Motor
  DHT1 = DHT22 Humidity and Temperature Sensor
  IC1 = Switching step-up voltage regulator [package=sot23-5]
  IC2 = Switching step-up voltage regulator [package=sot23-5]

nets:
  N1: U1.D0, Part1.TX2_LV
  N2: U1.D1, Part2.RX_LV
  N3: U1.D2, Part2.TX2_LV
  N4: U1.D4, Part3.TX2_LV
  N5: U1.D5, Part4.RX_LV
  N6: U1.D6, Part4.TX2_LV
  N7: U1.D7, Part1.RX_LV
  N8: U1.Vin, IC2.LX
  GND: U1.GND, IC2.GND
  N9: U2.PWM_SDA, U3.MAIN
  N10: U2.VDD, Part4.RX_HV
  N11: U3.COIL2, U6.COIL2, U8.COIL2, U7.COIL2, DHT1.VDD, IC1.LX
  N12: U3.NC, U5.COIL1, U6.NC, U8.NC, U7.NC, IC1.GND
  N13: U3.NO, Part4.TX2_HV
  N14: LED1.A, U7.MAIN
  N15: JP1.1, U8.MAIN
  N16: JP1.2, D1.A, U4.+, IC1.OUT, IC2.EN, IC2.OUT
  N17: D1.C, U4.-, U8.COIL1, IC1.NC, IC2.NC
  N18: U5.NO, Part1.TX2_HV
  N19: U5.MAIN, DHT1.GND
  N20: U6.NO, Part2.RX_HV
  N21: U6.MAIN, M1.pin_2
  N22: U8.NO, Part3.TX2_HV
  N23: U7.NO, Part2.TX2_HV
  N24: Part1.RX_HV, DHT1.DATA

notes:
  PIR Motion Sensor
  Light Control
  Fan Control
  Door Lock
  Dht22 Temperature & Humidity Sensor
  AC ~
  12V DC

custom parts:
  NodeMCU V1.0: ESP9266 based NodeMCU
