# Fritzing sketch rfid (saved by Fritzing 0.9.3b)

parts:
  U1 = NodeMCU V1.0
  U4 = LIPO-2000mAh [package=lipo-2000]
  IC2 = Switching step-up voltage regulator [package=sot23-5]
  Part1 = RFID-RC522-v2

nets:
  N1: U1.D4, Part1.SDA
  N2: U1.D5, Part1.SCK
  N3: U1.D6, Part1.MISO
  N4: U1.D7, Part1.MOSI
  N5: U1.D8, Part1.RST
  GND: U1.GND, IC2.GND, Part1.GND
  3V3: U1.3V3, Part1.3.3V
  N6: U1.Vin, IC2.LX
  N7: U4.+, IC2.EN, IC2.OUT
  N8: U4.-, IC2.NC

notes:
  RFID Reader
  12V DC

custom parts:
  NodeMCU V1.0: ESP9266 based NodeMCU
  RFID-RC522-v2: A simple China made RFID-RC522 Reader; do check the pin labels, as this is a MFRC522 based clone.
