# Fritzing sketch v2 (saved by Fritzing 0.9.3b)
breadboards: 1

parts:
  U1 = NodeMCU V1.0
  D1 = SOLAR-IXYS [package=solarbit-12x1]
  U4 = LIPO-2000mAh [package=lipo-2000]
  U5 = RELAY [package=relay-jzc]
  U7 = RELAY [package=relay-jzc]
  Part1 = Logic Level Converter
  Part2 = Logic Level Converter
  IC1 = Switching step-up voltage regulator [package=sot23-5]
  IC2 = Switching step-up voltage regulator [package=sot23-5]
  SW-1 = Vibration sensor module
  JP2 = Header 2 [package=jst-2-pth]

nets:
  N1: U1.D2, Part2.TX2_LV
  N2: U1.D4, Part1.RX_LV
  N3: U1.D5, Part1.TX2_LV
  N4: U1.Vin, IC2.LX
  GND: U1.GND, IC2.GND
  N5: D1.A, U4.+, U7.COIL1, IC1.OUT, IC2.EN, IC2.OUT
  N6: D1.C, U4.-, IC1.NC, IC2.NC, JP2.2
  N7: U5.NO, Part1.TX2_HV
  N8: U5.MAIN, SW-1.Ground
  N9: U5.COIL1, U7.NC, IC1.GND
  N10: U7.COIL2, IC1.LX, SW-1.vcc
  N11: U7.NO, Part2.TX2_HV
  N12: U7.MAIN, JP2.1
  N13: Part1.RX_HV, SW-1.Digital_output

notes:
  Door Lock
  Sound Sensor
  12V DC

custom parts:
  NodeMCU V1.0: ESP9266 based NodeMCU
  Vibration sensor module: Single-roller type full induction trigger switch. When no vibration or tilt, the product is ON conduction state, and in the steady state, when a vibration or tilt, the switch will be rendered instantly disconnect the conductive resistance increases, generating a current pulse signal, thereby triggering circuit. The default state of the swith is close Digital output Supply voltage:3.3V-5V On-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
