# Fritzing sketch v4 (saved by Fritzing 0.9.3b)
breadboards: 1

parts:
  U1 = NodeMCU V1.0
  D1 = SOLAR-IXYS [package=solarbit-12x1]
  U4 = LIPO-2000mAh [package=lipo-2000]
  U5 = RELAY [package=relay-jzc]
  U8 = RELAY [package=relay-jzc]
  U7 = RELAY [package=relay-jzc]
  Part1 = Logic Level Converter
  Part2 = Logic Level Converter
  Part3 = Logic Level Converter
  IC1 = Switching step-up voltage regulator [package=sot23-5]
  IC2 = Switching step-up voltage regulator [package=sot23-5]
  VALVE1 = Plastic Solenoid Valve
  Part4 = OpAmp Breakout
  RJ-2 = RJ-11 Connector with Breakout Board

nets:
  N1: U1.D2, Part2.TX2_LV
  N2: U1.D4, Part3.TX2_LV
  N3: U1.D5, U8.NO, Part3.GND
  N4: U1.D6, Part1.TX2_LV
  N5: U1.D7, Part1.RX_LV
  N6: U1.Vin, IC2.LX
  GND: U1.GND, IC2.GND
  N7: D1.A, U4.+, U7.COIL1, IC1.OUT, IC2.EN, IC2.OUT
  N8: D1.C, U4.-, IC1.NC, IC2.NC, VALVE1.no_name_yet#1
  N9: U5.NO, Part1.TX2_HV
  N10: U5.MAIN, Part4.GND
  N11: U5.COIL1, U8.NC, U8.COIL1, U7.NC, IC1.GND
  VCC: U8.COIL2, U7.COIL2, IC1.LX, Part4.VCC, RJ-2.Vcc
  N12: U8.MAIN, RJ-2.GND
  N13: U7.NO, Part2.TX2_HV
  N14: U7.MAIN, VALVE1.no_name_yet#2
  N15: Part1.RX_HV, Part4.OUT
  N16: Part3.TX2_HV, RJ-2.PRB

notes:
  Tank Valve
  Sound Sensor
  Water Level Sensor
  12V DC

custom parts:
  NodeMCU V1.0: ESP9266 based NodeMCU
