# Fritzing sketch v5 (saved by Fritzing 0.9.3b)
breadboards: 1

parts:
  U1 = NodeMCU V1.0
  D1 = SOLAR-IXYS [package=solarbit-12x1]
  U4 = LIPO-2000mAh [package=lipo-2000]
  U5 = RELAY [package=relay-jzc]
  Part1 = Logic Level Converter
  IC1 = Switching step-up voltage regulator [package=sot23-5]
  IC2 = Switching step-up voltage regulator [package=sot23-5]
  RJ-1 = RJ-11 Connector with Breakout Board

nets:
  N1: U1.D6, Part1.TX2_LV
  N2: U1.D7, Part1.RX_LV
  N3: U1.Vin, IC2.LX
  GND: U1.GND, IC2.GND
  N4: D1.A, U4.+, IC1.OUT, IC2.EN, IC2.OUT
  N5: D1.C, U4.-, IC1.NC, IC2.NC
  N6: U5.NO, Part1.TX2_HV
  N7: U5.MAIN, RJ-1.GND
  N8: U5.COIL1, IC1.GND
  N9: Part1.RX_HV, RJ-1.PRB
  N10: IC1.LX, RJ-1.Vcc

notes:
  Rain Sensor
  12V DC

custom parts:
  NodeMCU V1.0: ESP9266 based NodeMCU
